# Fritzing sketch 4x4x4CAD (saved by Fritzing 0.9.9b)
breadboards: 1

parts:
  Part2 = Arduino Mega 2560 (Rev3)  # not connected
  R1 = Resistor [tolerance=±5% power=0.25 resistance=100 package=THT]  # not connected
  LED14 = smd LED [color="Red (633nm)" package="1206 [SMD]"]
  LED5 = smd LED [color="Red (633nm)" package="1206 [SMD]"]
  LED12 = smd LED [color="Red (633nm)" package="1206 [SMD]"]
  LED9 = smd LED [color="Red (633nm)" package="1206 [SMD]"]
  LED6 = smd LED [color="Red (633nm)" package="1206 [SMD]"]
  LED18 = smd LED [color="Red (633nm)" package="1206 [SMD]"]
  LED8 = smd LED [color="Red (633nm)" package="1206 [SMD]"]
  LED16 = smd LED [color="Red (633nm)" package="1206 [SMD]"]
  LED19 = smd LED [color="Red (633nm)" package="1206 [SMD]"]
  LED20 = smd LED [color="Red (633nm)" package="1206 [SMD]"]
  LED21 = smd LED [color="Red (633nm)" package="1206 [SMD]"]
  LED22 = smd LED [color="Red (633nm)" package="1206 [SMD]"]
  LED23 = smd LED [color="Red (633nm)" package="1206 [SMD]"]
  LED24 = smd LED [color="Red (633nm)" package="1206 [SMD]"]
  LED25 = smd LED [color="Red (633nm)" package="1206 [SMD]"]
  LED26 = smd LED [color="Red (633nm)" package="1206 [SMD]"]
  LED27 = smd LED [color="Red (633nm)" package="1206 [SMD]"]
  LED28 = smd LED [color="Red (633nm)" package="1206 [SMD]"]
  LED29 = smd LED [color="Red (633nm)" package="1206 [SMD]"]
  LED30 = smd LED [color="Red (633nm)" package="1206 [SMD]"]
  LED31 = smd LED [color="Red (633nm)" package="1206 [SMD]"]
  LED32 = smd LED [color="Red (633nm)" package="1206 [SMD]"]
  LED33 = smd LED [color="Red (633nm)" package="1206 [SMD]"]
  LED34 = smd LED [color="Red (633nm)" package="1206 [SMD]"]
  LED35 = smd LED [color="Red (633nm)" package="1206 [SMD]"]
  LED37 = smd LED [color="Red (633nm)" package="1206 [SMD]"]
  LED38 = smd LED [color="Red (633nm)" package="1206 [SMD]"]
  LED39 = smd LED [color="Red (633nm)" package="1206 [SMD]"]
  LED40 = smd LED [color="Red (633nm)" package="1206 [SMD]"]
  LED41 = smd LED [color="Red (633nm)" package="1206 [SMD]"]
  LED42 = smd LED [color="Red (633nm)" package="1206 [SMD]"]
  LED36 = smd LED [color="Red (633nm)" package="1206 [SMD]"]

nets:
  N1: LED14.anode, LED5.anode, LED12.anode, LED9.anode, LED6.anode, LED18.anode, LED8.cathode, LED8.anode, LED16.anode, LED20.anode, LED21.anode, LED22.anode, LED23.anode
  N2: LED16.cathode, LED36.cathode
  N3: LED19.anode, LED24.anode, LED25.anode, LED26.anode
  N4: LED27.anode, LED28.anode, LED29.anode, LED30.anode, LED31.anode, LED32.anode, LED33.anode, LED34.anode, LED35.anode, LED37.anode, LED38.anode, LED39.anode, LED40.anode, LED41.anode, LED42.anode, LED36.anode
